// Logisim project (t3)类fib_s[x]=s[x-1]+(s[x-2]^s[x-3]).circ as structural Verilog: 1 circuit, main circuit main
module main (
  input  [4:0] in,
  output [31:0] out_2
);

  wire clk, comparator_1_eq, comparator_1_gt, en, \initial , or_1_out;
  wire [31:0] adder_1_out, and_1_out, bit_extender_1_out, counter_1_q, multiplexer_1_out, multiplexer_2_out,
       register_1_q, register_2_q, register_3_q;

  Clock clock_1 (.out(clk));
  Register #(.width(32)) register_1 (.D(adder_1_out), .en(en), .Q(register_1_q), .clk(clk), .clr(1'b0));
  Multiplexer #(.width(32), .enable("false")) multiplexer_1 (
    .in0(32'h1), .in1(register_1_q), .out(multiplexer_1_out), .sel(\initial ));
  Counter #(.width(32), .max('hffffffff)) counter_1 (
    .Q(counter_1_q), .clk(clk), .clr(1'b0));  // open: load, D, count, carry
  Register #(.width(32)) register_2 (.D(multiplexer_1_out), .en(en), .Q(register_2_q), .clk(clk), .clr(1'b0));
  assign bit_extender_1_out = {{27{1'b0}}, in};  // Bit_Extender bit_extender_1
  Multiplexer #(.width(32), .enable("false")) multiplexer_2 (
    .in0(32'h1), .in1(register_2_q), .out(multiplexer_2_out), .sel(\initial ));
  Comparator #(.width(32), .mode("unsigned")) comparator_1 (
    .a(counter_1_q), .b(bit_extender_1_out), .gt(comparator_1_gt), .eq(comparator_1_eq));  // open: lt
  Register #(.width(32)) register_3 (.D(multiplexer_2_out), .en(en), .Q(register_3_q), .clk(clk), .clr(1'b0));
  Multiplexer #(.width(32), .enable("false")) multiplexer_3 (
    .in0({32{1'b0}}), .in1(register_3_q), .out(out_2), .sel(\initial ));
  or or_1 (or_1_out, comparator_1_gt, comparator_1_eq);
  not not_1 (en, or_1_out);
  assign and_1_out = out_2 & multiplexer_2_out;  // AND_Gate and_1, 32 bits wide
  Adder #(.width(32)) adder_1 (.a(and_1_out), .b(multiplexer_1_out), .out(adder_1_out));  // open: cin, cout
  Counter #(.width(1), .max('h1), .ongoal("stay")) counter_2 (
    .Q(\initial ), .clk(clk), .clr(1'b0));  // open: load, D, count, carry

  // Notes on the sheet:
  //   s[x-1]
  //   s[x-2]
  //   s[x-3]
  //   s[x-3]
  //   s[x]
endmodule
