// Logisim project P0_L0_CRC.circ as structural Verilog: 5 circuits, main circuit mod2异或
module \mod2异或  (
  input  [10:0] in,
  input  [3:0] \除数 ,
  output [10:0] in_
);

  wire not_1_out, \判断最高位_1_判断 ;
  wire [3:0] xor_1_out;
  wire [10:0] shifter_1_out, shifter_2_out;

  Shifter #(.width(11)) shifter_1 (.in(in), .\dist (4'b0001), .out(shifter_1_out));
  assign xor_1_out = in[10:7] ^ \除数 ;  // XOR_Gate xor_1, 4 bits wide
  Shifter #(.width(11)) shifter_2 (.in({xor_1_out, in[6:0]}), .\dist (4'b0001), .out(shifter_2_out));
  \判断最高位  \u_判断最高位_1  (.in(in), .\判断 (\判断最高位_1_判断 ));
  Multiplexer #(.width(11)) multiplexer_1 (
    .in0(shifter_2_out), .in1(shifter_1_out), .out(in_), .sel(not_1_out));  // open: en
  not not_1 (not_1_out, \判断最高位_1_判断 );

  // Other names for the same wires on the sheet: 数据[10:0] = in
endmodule

module \判断最高位  (
  input  [10:0] in,
  output \判断 
);

  Comparator #(.width(1), .mode("unsigned")) comparator_1 (.a(in[10]), .b(1'b1), .eq(\判断 ));  // open: gt, lt
endmodule

module CRC (
  input  [7:0] A,
  input  [3:0] B,
  output [10:0] out_3
);

  wire [10:0] \mod2异或_1_in_ , \mod2异或_2_in_ , \mod2异或_3_in_ , \mod2异或_4_in_ , \mod2异或_5_in_ , \mod2异或_6_in_ ,
       \mod2异或_7_in_ , \mod2异或_8_in_ , \拓展位_1_数据 ;

  \拓展位  \u_拓展位_1  (.A(A), .\数据 (\拓展位_1_数据 ));
  \mod2异或  \mod2异或_1  (.in(\mod2异或_2_in_ ), .\除数 (B), .in_(\mod2异或_1_in_ ));
  \mod2异或  \mod2异或_2  (.in(\拓展位_1_数据 ), .\除数 (B), .in_(\mod2异或_2_in_ ));
  \mod2异或  \mod2异或_3  (.in(\mod2异或_1_in_ ), .\除数 (B), .in_(\mod2异或_3_in_ ));
  \mod2异或  \mod2异或_4  (.in(\mod2异或_3_in_ ), .\除数 (B), .in_(\mod2异或_4_in_ ));
  \mod2异或  \mod2异或_5  (.in(\mod2异或_4_in_ ), .\除数 (B), .in_(\mod2异或_5_in_ ));
  \mod2异或  \mod2异或_6  (.in(\mod2异或_5_in_ ), .\除数 (B), .in_(\mod2异或_6_in_ ));
  \mod2异或  \mod2异或_7  (.in(\mod2异或_6_in_ ), .\除数 (B), .in_(\mod2异或_7_in_ ));
  \mod2异或  \mod2异或_8  (.in(\mod2异或_7_in_ ), .\除数 (B), .in_(\mod2异或_8_in_ ));
  \输出  \u_输出_1  (.A(A), .\数据 (\mod2异或_8_in_ ), .C(out_3));
endmodule

module \拓展位  (
  input  [7:0] A,
  output [10:0] \数据 
);


  assign \数据  = {A, 3'b000};
endmodule

module \输出  (
  input  [7:0] A,
  input  [10:0] \数据 ,
  output [10:0] C
);


  assign C = {A, \数据 [10:8]};
endmodule
