// Logisim project P0_L0_FSM .circ as structural Verilog: 4 circuits, main circuit fsm
module fsm (
  input  clr,
  input  [1:0] \input ,
  output out_3
);

  wire clock_1_out, \状态储存_1_s0_2 , \状态储存_1_s1_2 , \状态转移_1_s0_2 , \状态转移_1_s1_2 ;

  \状态转移  \u_状态转移_1  (
    .s0(\状态储存_1_s0_2 ), .s1(\状态储存_1_s1_2 ), .in0(\input [0]), .in1(\input [1]), .clr(clr),
    .s0_2(\状态转移_1_s0_2 ), .s1_2(\状态转移_1_s1_2 ));
  Clock clock_1 (.out(clock_1_out));
  \状态储存  \u_状态储存_1  (
    .s0(\状态转移_1_s0_2 ), .s1(\状态转移_1_s1_2 ), .in_3(clock_1_out), .s0_2(\状态储存_1_s0_2 ), .s1_2(\状态储存_1_s1_2 ));
  \状态输出  \u_状态输出_1  (.s0(\状态储存_1_s0_2 ), .s1(\状态储存_1_s1_2 ), .in0(\input [0]), .in1(\input [1]), .out(out_3));
endmodule

module \状态转移  (
  input  s0,
  input  s1,
  input  in0,
  input  in1,
  input  clr,
  output s0_2,
  output s1_2
);

  wire and_1_out, and_2_out, and_3_out, and_4_out, not_1_out, not_2_out, not_3_out, not_4_out, not_5_out,
       not_6_out, not_7_out, not_8_out, not_9_out, not_10_out, not_11_out;

  not not_1 (not_1_out, in1);
  not not_2 (not_2_out, clr);
  not not_3 (not_3_out, s0);
  not not_4 (not_4_out, in0);
  not not_5 (not_5_out, clr);
  not not_6 (not_6_out, s0);
  not not_7 (not_7_out, in0);
  not not_8 (not_8_out, clr);
  not not_9 (not_9_out, s1);
  not not_10 (not_10_out, in0);
  not not_11 (not_11_out, clr);
  and and_1 (and_1_out, in0, not_1_out, not_2_out);
  and and_2 (and_2_out, not_3_out, s1, not_4_out, not_5_out);
  and and_3 (and_3_out, not_6_out, s1, not_7_out, not_8_out);
  and and_4 (and_4_out, s0, not_9_out, not_10_out, not_11_out);
  or or_1 (s0_2, and_1_out, and_2_out);
  or or_2 (s1_2, and_3_out, and_4_out);
endmodule

module \状态输出  (
  input  s0,
  input  s1,
  input  in0,
  input  in1,
  output out
);

  wire not_1_out, not_2_out;

  not not_1 (not_1_out, s0);
  and and_1 (out, not_1_out, s1, not_2_out);
  not not_2 (not_2_out, in0);
endmodule

module \状态储存  (
  input  s0,
  input  s1,
  input  in_3,
  output s0_2,
  output s1_2
);

  Register #(.width(2)) register_1 (.D({s1, s0}), .Q({s1_2, s0_2}), .clk(in_3));  // open: en, clr
endmodule
