// Logisim project P0_L0_GRF.circ as structural Verilog: 1 circuit, main circuit grf
module grf (
  input  in_1,
  input  in_2,
  input  in_3,
  input  [4:0] in_4,
  input  [4:0] in_5,
  input  [4:0] in_6,
  input  [31:0] in_7,
  output [31:0] out_8,
  output [31:0] out_9
);

  wire str0, str1, str2, str3, str4, str5, str6, str7, str8, str9, str10, str11, str12, str13, str14, str15,
       str16, str17, str18, str19, str20, str21, str22, str23, str24, str25, str26, str27, str28, str29,
       str30, str31;
  wire [31:0] in_data0, in_data1, in_data2, in_data3, in_data4, in_data5, in_data6, in_data7, in_data8,
       in_data9, in_data10, in_data11, in_data12, in_data13, in_data14, in_data15, in_data16, in_data17,
       in_data18, in_data19, in_data20, in_data21, in_data22, in_data23, in_data24, in_data25, in_data26,
       in_data27, in_data28, in_data29, in_data30, in_data31, out_data0, out_data1, out_data2, out_data3,
       out_data4, out_data5, out_data6, out_data7, out_data8, out_data9, out_data10, out_data11, out_data12,
       out_data13, out_data14, out_data15, out_data16, out_data17, out_data18, out_data19, out_data20,
       out_data21, out_data22, out_data23, out_data24, out_data25, out_data26, out_data27, out_data28,
       out_data29, out_data30, out_data31;

  Demultiplexer #(.select(5), .width(32), .enable("false")) demultiplexer_1 (
    .out0(in_data0), .out1(in_data1), .out2(in_data2), .out3(in_data3), .out4(in_data4), .out5(in_data5),
    .out6(in_data6), .out7(in_data7), .out8(in_data8), .out9(in_data9), .out10(in_data10), .out11(in_data11),
    .out12(in_data12), .out13(in_data13), .out14(in_data14), .out15(in_data15), .out16(in_data16),
    .out17(in_data17), .out18(in_data18), .out19(in_data19), .out20(in_data20), .out21(in_data21),
    .out22(in_data22), .out23(in_data23), .out24(in_data24), .out25(in_data25), .out26(in_data26),
    .out27(in_data27), .out28(in_data28), .out29(in_data29), .out30(in_data30), .out31(in_data31), .in(in_7),
    .sel(in_6));
  Register #(.width(32)) _0 (.D(in_data0), .en(str0), .Q(out_data0), .clk(in_1), .clr(1'b1));
  Register #(.width(32)) _4 (.D(in_data4), .en(str4), .Q(out_data4), .clk(in_1), .clr(in_2));
  Register #(.width(32)) _8 (.D(in_data8), .en(str8), .Q(out_data8), .clk(in_1), .clr(in_2));
  Register #(.width(32)) _12 (.D(in_data12), .en(str12), .Q(out_data12), .clk(in_1), .clr(in_2));
  Register #(.width(32)) _16 (.D(in_data16), .en(str16), .Q(out_data16), .clk(in_1), .clr(in_2));
  Register #(.width(32)) _20 (.D(in_data20), .en(str20), .Q(out_data20), .clk(in_1), .clr(in_2));
  Register #(.width(32)) _24 (.D(in_data24), .en(str24), .Q(out_data24), .clk(in_1), .clr(in_2));
  Register #(.width(32)) _28 (.D(in_data28), .en(str28), .Q(out_data28), .clk(in_1), .clr(in_2));
  Register #(.width(32)) _21 (.D(in_data21), .en(str21), .Q(out_data21), .clk(in_1), .clr(in_2));
  Register #(.width(32)) _25 (.D(in_data25), .en(str25), .Q(out_data25), .clk(in_1), .clr(in_2));
  Register #(.width(32)) _29 (.D(in_data29), .en(str29), .Q(out_data29), .clk(in_1), .clr(in_2));
  Register #(.width(32)) _1 (.D(in_data1), .en(str1), .Q(out_data1), .clk(in_1), .clr(in_2));
  Register #(.width(32)) _5 (.D(in_data5), .en(str5), .Q(out_data5), .clk(in_1), .clr(in_2));
  Register #(.width(32)) _9 (.D(in_data9), .en(str9), .Q(out_data9), .clk(in_1), .clr(in_2));
  Register #(.width(32)) _13 (.D(in_data13), .en(str13), .Q(out_data13), .clk(in_1), .clr(in_2));
  Register #(.width(32)) _17 (.D(in_data17), .en(str17), .Q(out_data17), .clk(in_1), .clr(in_2));
  Demultiplexer #(.select(5), .enable("false")) demultiplexer_2 (
    .out0(str0), .out1(str1), .out2(str2), .out3(str3), .out4(str4), .out5(str5), .out6(str6), .out7(str7),
    .out8(str8), .out9(str9), .out10(str10), .out11(str11), .out12(str12), .out13(str13), .out14(str14),
    .out15(str15), .out16(str16), .out17(str17), .out18(str18), .out19(str19), .out20(str20), .out21(str21),
    .out22(str22), .out23(str23), .out24(str24), .out25(str25), .out26(str26), .out27(str27), .out28(str28),
    .out29(str29), .out30(str30), .out31(str31), .in(in_3), .sel(in_6));
  Multiplexer #(.select(5), .width(32), .enable("false")) multiplexer_1 (
    .in0(out_data0), .in1(out_data1), .in2(out_data2), .in3(out_data3), .in4(out_data4), .in5(out_data5),
    .in6(out_data6), .in7(out_data7), .in8(out_data8), .in9(out_data9), .in10(out_data10), .in11(out_data11),
    .in12(out_data12), .in13(out_data13), .in14(out_data14), .in15(out_data15), .in16(out_data16),
    .in17(out_data17), .in18(out_data18), .in19(out_data19), .in20(out_data20), .in21(out_data21),
    .in22(out_data22), .in23(out_data23), .in24(out_data24), .in25(out_data25), .in26(out_data26),
    .in27(out_data27), .in28(out_data28), .in29(out_data29), .in30(out_data30), .in31(out_data31),
    .out(out_8), .sel(in_4));
  Multiplexer #(.select(5), .width(32), .enable("false")) multiplexer_2 (
    .in0(out_data0), .in1(out_data1), .in2(out_data2), .in3(out_data3), .in4(out_data4), .in5(out_data5),
    .in6(out_data6), .in7(out_data7), .in8(out_data8), .in9(out_data9), .in10(out_data10), .in11(out_data11),
    .in12(out_data12), .in13(out_data13), .in14(out_data14), .in15(out_data15), .in16(out_data16),
    .in17(out_data17), .in18(out_data18), .in19(out_data19), .in20(out_data20), .in21(out_data21),
    .in22(out_data22), .in23(out_data23), .in24(out_data24), .in25(out_data25), .in26(out_data26),
    .in27(out_data27), .in28(out_data28), .in29(out_data29), .in30(out_data30), .in31(out_data31),
    .out(out_9), .sel(in_5));
  Pull_Resistor pull_resistor_1 (.node(str18));
  Register #(.width(32)) _2 (.D(in_data2), .en(str2), .Q(out_data2), .clk(in_1), .clr(in_2));
  Register #(.width(32)) _6 (.D(in_data6), .en(str6), .Q(out_data6), .clk(in_1), .clr(in_2));
  Register #(.width(32)) _10 (.D(in_data10), .en(str10), .Q(out_data10), .clk(in_1), .clr(in_2));
  Register #(.width(32)) _14 (.D(in_data14), .en(str14), .Q(out_data14), .clk(in_1), .clr(in_2));
  Register #(.width(32)) _18 (.D(in_data18), .en(str18), .Q(out_data18), .clk(in_1), .clr(in_2));
  Register #(.width(32)) _22 (.D(in_data22), .en(str22), .Q(out_data22), .clk(in_1), .clr(in_2));
  Register #(.width(32)) _26 (.D(in_data26), .en(str26), .Q(out_data26), .clk(in_1), .clr(in_2));
  Register #(.width(32)) _30 (.D(in_data30), .en(str30), .Q(out_data30), .clk(in_1), .clr(in_2));
  Pull_Resistor pull_resistor_2 (.node(str0));
  Pull_Resistor pull_resistor_3 (.node(str1));
  Pull_Resistor pull_resistor_4 (.node(str2));
  Pull_Resistor pull_resistor_5 (.node(str3));
  Pull_Resistor pull_resistor_6 (.node(str4));
  Pull_Resistor pull_resistor_7 (.node(str5));
  Pull_Resistor pull_resistor_8 (.node(str6));
  Pull_Resistor pull_resistor_9 (.node(str7));
  Pull_Resistor pull_resistor_10 (.node(str8));
  Pull_Resistor pull_resistor_11 (.node(str9));
  Pull_Resistor pull_resistor_12 (.node(str10));
  Pull_Resistor pull_resistor_13 (.node(str15));
  Pull_Resistor pull_resistor_14 (.node(str16));
  Pull_Resistor pull_resistor_15 (.node(str17));
  Pull_Resistor pull_resistor_16 (.node(str19));
  Pull_Resistor pull_resistor_17 (.node(str20));
  Pull_Resistor pull_resistor_18 (.node(str21));
  Pull_Resistor pull_resistor_19 (.node(str22));
  Pull_Resistor pull_resistor_20 (.node(str23));
  Pull_Resistor pull_resistor_21 (.node(str24));
  Pull_Resistor pull_resistor_22 (.node(str25));
  Pull_Resistor pull_resistor_23 (.node(str26));
  Pull_Resistor pull_resistor_24 (.node(str27));
  Pull_Resistor pull_resistor_25 (.node(str28));
  Pull_Resistor pull_resistor_26 (.node(str29));
  Pull_Resistor pull_resistor_27 (.node(str30));
  Pull_Resistor pull_resistor_28 (.node(str31));
  Pull_Resistor pull_resistor_29 (.node(str11));
  Pull_Resistor pull_resistor_30 (.node(str12));
  Pull_Resistor pull_resistor_31 (.node(str13));
  Pull_Resistor pull_resistor_32 (.node(str14));
  Register #(.width(32)) _3 (.D(in_data3), .en(str3), .Q(out_data3), .clk(in_1), .clr(in_2));
  Register #(.width(32)) _7 (.D(in_data7), .en(str7), .Q(out_data7), .clk(in_1), .clr(in_2));
  Register #(.width(32)) _11 (.D(in_data11), .en(str11), .Q(out_data11), .clk(in_1), .clr(in_2));
  Register #(.width(32)) _15 (.D(in_data15), .en(str15), .Q(out_data15), .clk(in_1), .clr(in_2));
  Register #(.width(32)) _19 (.D(in_data19), .en(str19), .Q(out_data19), .clk(in_1), .clr(in_2));
  Register #(.width(32)) _23 (.D(in_data23), .en(str23), .Q(out_data23), .clk(in_1), .clr(in_2));
  Register #(.width(32)) _27 (.D(in_data27), .en(str27), .Q(out_data27), .clk(in_1), .clr(in_2));
  Register #(.width(32)) _31 (.D(in_data31), .en(str31), .Q(out_data31), .clk(in_1), .clr(in_2));

  // Other names for the same wires on the sheet: A1[4:0] = in_4; A2[4:0] = in_5; A3[4:0] = in_6; clk = in_1;
  //   RD1[31:0] = out_8; RD2[31:0] = out_9; reset = in_2; WD[31:0] = in_7; WE = in_3
endmodule
