// Logisim project P0_L1_ftoi.circ as structural Verilog: 4 circuits, main circuit ftoi
module ftoi (
  input  [15:0] float,
  output [31:0] \int 
);

  wire or_1_out, \判断1_1_out_2 , \判断2_1_out_2 ;
  wire [31:0] \计算_1_out_2 ;

  \计算  \u_计算_1  (.float(float), .out_2(\计算_1_out_2 ));
  \判断1  \u_判断1_1  (.float(float), .out_2(\判断1_1_out_2 ));
  \判断2  \u_判断2_1  (.float(float), .out_2(\判断2_1_out_2 ));
  Multiplexer #(.width(32)) multiplexer_1 (
    .in0(\计算_1_out_2 ), .in1({32{1'b0}}), .out(\int ), .sel(or_1_out));  // open: en
  or or_1 (or_1_out, \判断1_1_out_2 , \判断2_1_out_2 );
endmodule

module \判断1  (
  input  [15:0] float,
  output out_2
);

  Comparator #(.width(5), .mode("unsigned")) comparator_1 (
    .a(float[14:10]), .b({5{1'b0}}), .eq(out_2));  // open: gt, lt
endmodule

module \计算  (
  input  [15:0] float,
  output [31:0] out_2
);

  wire comparator_1_eq;
  wire [4:0] subtractor_1_out;
  wire [31:0] bit_extender_1_out, bit_extender_2_out, multiplexer_1_out, shifter_1_out;

  Comparator #(.width(1), .mode("unsigned")) comparator_1 (
    .a(float[15]), .b(1'b1), .eq(comparator_1_eq));  // open: gt, lt
  Multiplexer #(.width(32)) multiplexer_1 (
    .in0(32'h1), .in1({32{1'b1}}), .out(multiplexer_1_out), .sel(comparator_1_eq));  // open: en
  Subtractor #(.width(5)) subtractor_1 (.a(float[14:10]), .b(5'b01111), .out(subtractor_1_out));  // open: bin, bout
  assign bit_extender_1_out = {{21{1'b0}}, {1'b1, float[9:0]}};  // Bit_Extender bit_extender_1
  Shifter #(.width(32)) shifter_1 (.in(bit_extender_1_out), .\dist (subtractor_1_out), .out(shifter_1_out));
  assign bit_extender_2_out = {{10{1'b0}}, shifter_1_out[31:10]};  // Bit_Extender bit_extender_2
  Multiplier #(.width(32)) multiplier_1 (
    .a(bit_extender_2_out), .b(multiplexer_1_out), .out(out_2));  // open: cin, cout
endmodule

module \判断2  (
  input  [15:0] float,
  output out_2
);

  wire [4:0] subtractor_1_out;

  Subtractor #(.width(5)) subtractor_1 (.a(float[14:10]), .b(5'b01111), .out(subtractor_1_out));  // open: bin, bout
  // Probe on subtractor_1_out
  Comparator #(.width(5)) comparator_1 (.a({5{1'b0}}), .b(subtractor_1_out), .gt(out_2));  // open: eq, lt
endmodule
