// Logisim project P0_L1_navigation_2020.circ as structural Verilog: 4 circuits, main circuit navigation
module navigation (
  input  [1:0] dir,
  input  clk,
  input  reset,
  output arrive,
  output hit
);

  wire [3:0] \状态储存_1_out_4 , \状态转移_1_s02 ;

  \状态转移  \u_状态转移_1  (
    .s3(\状态储存_1_out_4 [3]), .s2(\状态储存_1_out_4 [2]), .s1(\状态储存_1_out_4 [1]), .s0(\状态储存_1_out_4 [0]),
    .in1(dir[1]), .in0(dir[0]), .s32(\状态转移_1_s02 [3]), .s22(\状态转移_1_s02 [2]), .s12(\状态转移_1_s02 [1]),
    .s02(\状态转移_1_s02 [0]));
  \状态储存  \u_状态储存_1  (.in_1(\状态转移_1_s02 ), .clk(clk), .reset(reset), .out_4(\状态储存_1_out_4 ));
  \状态输出  \u_状态输出_1  (
    .s3(\状态储存_1_out_4 [3]), .s2(\状态储存_1_out_4 [2]), .s1(\状态储存_1_out_4 [1]), .s0(\状态储存_1_out_4 [0]),
    .arrive(arrive), .hit(hit));
endmodule

module \状态转移  (
  input  s3,
  input  s2,
  input  s1,
  input  s0,
  input  in1,
  input  in0,
  output s32,
  output s22,
  output s12,
  output s02
);

  wire and_1_out, and_2_out, and_3_out, and_4_out, and_5_out, and_6_out, and_7_out, and_8_out, and_9_out,
       and_10_out, and_11_out, and_12_out, and_13_out, and_14_out, and_15_out, and_16_out, and_17_out,
       and_18_out, and_19_out, and_20_out, and_21_out, and_22_out, and_23_out, and_24_out, and_25_out,
       and_26_out, and_27_out, and_28_out, not_1_out, not_2_out, not_3_out, not_4_out, not_5_out, not_6_out,
       not_7_out, not_8_out, not_9_out, not_10_out, not_11_out, not_12_out, not_13_out, not_14_out,
       not_15_out, not_16_out, not_17_out, not_18_out, not_19_out, not_20_out, not_21_out, not_22_out,
       not_23_out, not_24_out, not_25_out, not_26_out, not_27_out, not_28_out, not_29_out, not_30_out,
       not_31_out, not_32_out, not_33_out, not_34_out, not_35_out, not_36_out, not_37_out, not_38_out,
       not_39_out, not_40_out, not_41_out, not_42_out, not_43_out, not_44_out, not_45_out, not_46_out,
       not_47_out, not_48_out, not_49_out, not_50_out;

  not not_1 (not_1_out, s2);
  not not_2 (not_2_out, in1);
  not not_3 (not_3_out, in0);
  not not_4 (not_4_out, s2);
  not not_5 (not_5_out, s2);
  not not_6 (not_6_out, s1);
  not not_7 (not_7_out, s0);
  not not_8 (not_8_out, in1);
  not not_9 (not_9_out, in0);
  not not_10 (not_10_out, s2);
  not not_11 (not_11_out, s0);
  not not_12 (not_12_out, in1);
  not not_13 (not_13_out, s3);
  not not_14 (not_14_out, s2);
  not not_15 (not_15_out, s1);
  not not_16 (not_16_out, s0);
  not not_17 (not_17_out, s1);
  not not_18 (not_18_out, s0);
  not not_19 (not_19_out, in1);
  not not_20 (not_20_out, s0);
  not not_21 (not_21_out, in0);
  not not_22 (not_22_out, s2);
  not not_23 (not_23_out, in1);
  not not_24 (not_24_out, s1);
  not not_25 (not_25_out, s1);
  not not_26 (not_26_out, s2);
  not not_27 (not_27_out, s1);
  not not_28 (not_28_out, in1);
  not not_29 (not_29_out, s2);
  not not_30 (not_30_out, s1);
  not not_31 (not_31_out, s0);
  not not_32 (not_32_out, in1);
  not not_33 (not_33_out, s0);
  not not_34 (not_34_out, in0);
  not not_35 (not_35_out, in1);
  not not_36 (not_36_out, s3);
  not not_37 (not_37_out, s2);
  not not_38 (not_38_out, s1);
  not not_39 (not_39_out, s0);
  not not_40 (not_40_out, s1);
  not not_41 (not_41_out, in1);
  not not_42 (not_42_out, in0);
  not not_43 (not_43_out, s1);
  not not_44 (not_44_out, s0);
  not not_45 (not_45_out, s2);
  not not_46 (not_46_out, in0);
  not not_47 (not_47_out, s1);
  not not_48 (not_48_out, in1);
  not not_49 (not_49_out, in0);
  not not_50 (not_50_out, in0);
  and and_1 (and_1_out, not_1_out, s1, s0, not_2_out, not_3_out);
  and and_2 (and_2_out, not_4_out, s1, s0, in1, in0);
  and and_3 (and_3_out, s3, not_5_out, not_6_out, not_7_out, not_8_out, not_9_out);
  and and_4 (and_4_out, s3, in1, in0);
  and and_5 (and_5_out, not_10_out, not_11_out, not_12_out, in0);
  and and_6 (and_6_out, not_13_out, not_14_out, not_15_out, not_16_out, in1);
  and and_7 (and_7_out, not_17_out, s0, in1, in0);
  and and_8 (and_8_out, s1, not_18_out, not_19_out);
  and and_9 (and_9_out, s1, not_20_out, not_21_out);
  and and_10 (and_10_out, not_22_out, s1, not_23_out, in0);
  and and_11 (and_11_out, s2, not_24_out, s0, in0);
  and and_12 (and_12_out, s2, not_25_out, s0, in1);
  and and_13 (and_13_out, s2, s0, in1, in0);
  and and_14 (and_14_out, not_26_out, not_27_out, s0, not_28_out);
  and and_15 (and_15_out, not_29_out, not_30_out, s0, in0);
  and and_16 (and_16_out, s1, not_31_out, not_32_out, in0);
  and and_17 (and_17_out, s1, not_33_out, in1, not_34_out);
  and and_18 (and_18_out, s2, s1, s0, not_35_out);
  and and_19 (and_19_out, s2, s1, s0, in0);
  and and_20 (and_20_out, not_36_out, not_37_out, not_38_out, not_39_out);
  and and_21 (and_21_out, not_40_out, s0, not_41_out, not_42_out);
  and and_22 (and_22_out, not_43_out, s0, in1, in0);
  and and_23 (and_23_out, s1, not_44_out, in1, in0);
  and and_24 (and_24_out, not_45_out, s1, s0, in1, not_46_out);
  and and_25 (and_25_out, s2, not_47_out, s0);
  and and_26 (and_26_out, s2, s0, not_48_out, not_49_out);
  and and_27 (and_27_out, s2, s1, in1, in0);
  and and_28 (and_28_out, s3, in1, not_50_out);
  or or_1 (s32, and_1_out, and_2_out, and_3_out, and_4_out);
  or or_2 (s22, and_5_out, and_6_out, and_7_out, and_8_out, and_9_out, and_10_out, and_11_out, and_12_out, and_13_out);
  or or_3 (s12, and_14_out, and_15_out, and_16_out, and_17_out, and_18_out, and_19_out);
  or or_4 (s02, and_20_out, and_21_out, and_22_out, and_23_out, and_24_out, and_25_out, and_26_out, and_27_out, and_28_out);
endmodule

module \状态储存  (
  input  [3:0] in_1,
  input  clk,
  input  reset,
  output [3:0] out_4
);

  Register #(.width(4)) register_1 (.D(in_1), .Q(out_4), .clk(clk), .clr(reset));  // open: en
endmodule

module \状态输出  (
  input  s3,
  input  s2,
  input  s1,
  input  s0,
  output arrive,
  output hit
);

  wire and_2_out, and_3_out, not_1_out, not_2_out;

  not not_1 (not_1_out, s1);
  and and_1 (arrive, s2, not_1_out, not_2_out);
  not not_2 (not_2_out, s0);
  and and_2 (and_2_out, s2, s0);
  and and_3 (and_3_out, s2, s1);
  or or_1 (hit, and_2_out, and_3_out, s3);
endmodule
