// Logisim project src.circ as structural Verilog: 9 circuits, main circuit main
module GRF (
  input  clk,
  input  reset,
  input  WE,
  input  [4:0] A1,
  input  [4:0] A2,
  input  [4:0] A3,
  input  [31:0] WD,
  output [31:0] RD1,
  output [31:0] RD2
);

  wire str0, str1, str2, str3, str4, str5, str6, str7, str8, str9, str10, str11, str12, str13, str14, str15,
       str16, str17, str18, str19, str20, str21, str22, str23, str24, str25, str26, str27, str28, str29,
       str30, str31;
  wire [31:0] in_data0, in_data1, in_data2, in_data3, in_data4, in_data5, in_data6, in_data7, in_data8,
       in_data9, in_data10, in_data11, in_data12, in_data13, in_data14, in_data15, in_data16, in_data17,
       in_data18, in_data19, in_data20, in_data21, in_data22, in_data23, in_data24, in_data25, in_data26,
       in_data27, in_data28, in_data29, in_data30, in_data31, out_data0, out_data1, out_data2, out_data3,
       out_data4, out_data5, out_data6, out_data7, out_data8, out_data9, out_data10, out_data11, out_data12,
       out_data13, out_data14, out_data15, out_data16, out_data17, out_data18, out_data19, out_data20,
       out_data21, out_data22, out_data23, out_data24, out_data25, out_data26, out_data27, out_data28,
       out_data29, out_data30, out_data31;

  Demultiplexer #(.select(5), .width(32), .enable("false")) demultiplexer_1 (
    .out0(in_data0), .out1(in_data1), .out2(in_data2), .out3(in_data3), .out4(in_data4), .out5(in_data5),
    .out6(in_data6), .out7(in_data7), .out8(in_data8), .out9(in_data9), .out10(in_data10), .out11(in_data11),
    .out12(in_data12), .out13(in_data13), .out14(in_data14), .out15(in_data15), .out16(in_data16),
    .out17(in_data17), .out18(in_data18), .out19(in_data19), .out20(in_data20), .out21(in_data21),
    .out22(in_data22), .out23(in_data23), .out24(in_data24), .out25(in_data25), .out26(in_data26),
    .out27(in_data27), .out28(in_data28), .out29(in_data29), .out30(in_data30), .out31(in_data31), .in(WD),
    .sel(A3));
  Register #(.width(32)) _0 (.D(in_data0), .en(str0), .Q(out_data0), .clk(clk), .clr(1'b1));
  Register #(.width(32)) _4 (.D(in_data4), .en(str4), .Q(out_data4), .clk(clk), .clr(reset));
  Register #(.width(32)) _8 (.D(in_data8), .en(str8), .Q(out_data8), .clk(clk), .clr(reset));
  Register #(.width(32)) _12 (.D(in_data12), .en(str12), .Q(out_data12), .clk(clk), .clr(reset));
  Register #(.width(32)) _16 (.D(in_data16), .en(str16), .Q(out_data16), .clk(clk), .clr(reset));
  Register #(.width(32)) _20 (.D(in_data20), .en(str20), .Q(out_data20), .clk(clk), .clr(reset));
  Register #(.width(32)) _24 (.D(in_data24), .en(str24), .Q(out_data24), .clk(clk), .clr(reset));
  Register #(.width(32)) _28 (.D(in_data28), .en(str28), .Q(out_data28), .clk(clk), .clr(reset));
  Register #(.width(32)) _21 (.D(in_data21), .en(str21), .Q(out_data21), .clk(clk), .clr(reset));
  Register #(.width(32)) _25 (.D(in_data25), .en(str25), .Q(out_data25), .clk(clk), .clr(reset));
  Register #(.width(32)) _29 (.D(in_data29), .en(str29), .Q(out_data29), .clk(clk), .clr(reset));
  Register #(.width(32)) _1 (.D(in_data1), .en(str1), .Q(out_data1), .clk(clk), .clr(reset));
  Register #(.width(32)) _5 (.D(in_data5), .en(str5), .Q(out_data5), .clk(clk), .clr(reset));
  Register #(.width(32)) _9 (.D(in_data9), .en(str9), .Q(out_data9), .clk(clk), .clr(reset));
  Register #(.width(32)) _13 (.D(in_data13), .en(str13), .Q(out_data13), .clk(clk), .clr(reset));
  Register #(.width(32)) _17 (.D(in_data17), .en(str17), .Q(out_data17), .clk(clk), .clr(reset));
  Demultiplexer #(.select(5), .enable("false")) demultiplexer_2 (
    .out0(str0), .out1(str1), .out2(str2), .out3(str3), .out4(str4), .out5(str5), .out6(str6), .out7(str7),
    .out8(str8), .out9(str9), .out10(str10), .out11(str11), .out12(str12), .out13(str13), .out14(str14),
    .out15(str15), .out16(str16), .out17(str17), .out18(str18), .out19(str19), .out20(str20), .out21(str21),
    .out22(str22), .out23(str23), .out24(str24), .out25(str25), .out26(str26), .out27(str27), .out28(str28),
    .out29(str29), .out30(str30), .out31(str31), .in(WE), .sel(A3));
  Multiplexer #(.select(5), .width(32), .enable("false")) multiplexer_1 (
    .in0(out_data0), .in1(out_data1), .in2(out_data2), .in3(out_data3), .in4(out_data4), .in5(out_data5),
    .in6(out_data6), .in7(out_data7), .in8(out_data8), .in9(out_data9), .in10(out_data10), .in11(out_data11),
    .in12(out_data12), .in13(out_data13), .in14(out_data14), .in15(out_data15), .in16(out_data16),
    .in17(out_data17), .in18(out_data18), .in19(out_data19), .in20(out_data20), .in21(out_data21),
    .in22(out_data22), .in23(out_data23), .in24(out_data24), .in25(out_data25), .in26(out_data26),
    .in27(out_data27), .in28(out_data28), .in29(out_data29), .in30(out_data30), .in31(out_data31), .out(RD1),
    .sel(A1));
  Multiplexer #(.select(5), .width(32), .enable("false")) multiplexer_2 (
    .in0(out_data0), .in1(out_data1), .in2(out_data2), .in3(out_data3), .in4(out_data4), .in5(out_data5),
    .in6(out_data6), .in7(out_data7), .in8(out_data8), .in9(out_data9), .in10(out_data10), .in11(out_data11),
    .in12(out_data12), .in13(out_data13), .in14(out_data14), .in15(out_data15), .in16(out_data16),
    .in17(out_data17), .in18(out_data18), .in19(out_data19), .in20(out_data20), .in21(out_data21),
    .in22(out_data22), .in23(out_data23), .in24(out_data24), .in25(out_data25), .in26(out_data26),
    .in27(out_data27), .in28(out_data28), .in29(out_data29), .in30(out_data30), .in31(out_data31), .out(RD2),
    .sel(A2));
  Pull_Resistor pull_resistor_1 (.node(str18));
  Register #(.width(32)) _2 (.D(in_data2), .en(str2), .Q(out_data2), .clk(clk), .clr(reset));
  Register #(.width(32)) _6 (.D(in_data6), .en(str6), .Q(out_data6), .clk(clk), .clr(reset));
  Register #(.width(32)) _10 (.D(in_data10), .en(str10), .Q(out_data10), .clk(clk), .clr(reset));
  Register #(.width(32)) _14 (.D(in_data14), .en(str14), .Q(out_data14), .clk(clk), .clr(reset));
  Register #(.width(32)) _18 (.D(in_data18), .en(str18), .Q(out_data18), .clk(clk), .clr(reset));
  Register #(.width(32)) _22 (.D(in_data22), .en(str22), .Q(out_data22), .clk(clk), .clr(reset));
  Register #(.width(32)) _26 (.D(in_data26), .en(str26), .Q(out_data26), .clk(clk), .clr(reset));
  Register #(.width(32)) _30 (.D(in_data30), .en(str30), .Q(out_data30), .clk(clk), .clr(reset));
  Pull_Resistor pull_resistor_2 (.node(str0));
  Pull_Resistor pull_resistor_3 (.node(str1));
  Pull_Resistor pull_resistor_4 (.node(str2));
  Pull_Resistor pull_resistor_5 (.node(str3));
  Pull_Resistor pull_resistor_6 (.node(str4));
  Pull_Resistor pull_resistor_7 (.node(str5));
  Pull_Resistor pull_resistor_8 (.node(str6));
  Pull_Resistor pull_resistor_9 (.node(str7));
  Pull_Resistor pull_resistor_10 (.node(str8));
  Pull_Resistor pull_resistor_11 (.node(str9));
  Pull_Resistor pull_resistor_12 (.node(str10));
  Pull_Resistor pull_resistor_13 (.node(str15));
  Pull_Resistor pull_resistor_14 (.node(str16));
  Pull_Resistor pull_resistor_15 (.node(str17));
  Pull_Resistor pull_resistor_16 (.node(str19));
  Pull_Resistor pull_resistor_17 (.node(str20));
  Pull_Resistor pull_resistor_18 (.node(str21));
  Pull_Resistor pull_resistor_19 (.node(str22));
  Pull_Resistor pull_resistor_20 (.node(str23));
  Pull_Resistor pull_resistor_21 (.node(str24));
  Pull_Resistor pull_resistor_22 (.node(str25));
  Pull_Resistor pull_resistor_23 (.node(str26));
  Pull_Resistor pull_resistor_24 (.node(str27));
  Pull_Resistor pull_resistor_25 (.node(str28));
  Pull_Resistor pull_resistor_26 (.node(str29));
  Pull_Resistor pull_resistor_27 (.node(str30));
  Pull_Resistor pull_resistor_28 (.node(str31));
  Pull_Resistor pull_resistor_29 (.node(str11));
  Pull_Resistor pull_resistor_30 (.node(str12));
  Pull_Resistor pull_resistor_31 (.node(str13));
  Pull_Resistor pull_resistor_32 (.node(str14));
  Register #(.width(32)) _3 (.D(in_data3), .en(str3), .Q(out_data3), .clk(clk), .clr(reset));
  Register #(.width(32)) _7 (.D(in_data7), .en(str7), .Q(out_data7), .clk(clk), .clr(reset));
  Register #(.width(32)) _11 (.D(in_data11), .en(str11), .Q(out_data11), .clk(clk), .clr(reset));
  Register #(.width(32)) _15 (.D(in_data15), .en(str15), .Q(out_data15), .clk(clk), .clr(reset));
  Register #(.width(32)) _19 (.D(in_data19), .en(str19), .Q(out_data19), .clk(clk), .clr(reset));
  Register #(.width(32)) _23 (.D(in_data23), .en(str23), .Q(out_data23), .clk(clk), .clr(reset));
  Register #(.width(32)) _27 (.D(in_data27), .en(str27), .Q(out_data27), .clk(clk), .clr(reset));
  Register #(.width(32)) _31 (.D(in_data31), .en(str31), .Q(out_data31), .clk(clk), .clr(reset));
endmodule

module ALU (
  input  [3:0] ALUControl,
  input  [31:0] SrcA,
  input  [31:0] SrcB,
  input  [4:0] shamt,
  output [31:0] Result,
  output ALUZero
);

  wire comparator_1_eq, comparator_2_lt;
  wire [31:0] adder_1_out, bit_extender_1_out, bit_extender_2_out, or_1_out, shifter_1_out, shifter_2_out,
       subtractor_1_out;

  Adder #(.width(32)) adder_1 (.a(SrcA), .b(SrcB), .out(adder_1_out));  // open: cin, cout
  Subtractor #(.width(32)) subtractor_1 (.a(SrcA), .b(SrcB), .out(subtractor_1_out));  // open: bin, bout
  assign or_1_out = SrcA | SrcB;  // OR_Gate or_1, 32 bits wide
  Comparator #(.width(32), .mode("unsigned")) comparator_1 (.a(SrcA), .b(SrcB), .eq(comparator_1_eq));  // open: gt, lt
  assign bit_extender_1_out = {{31{1'b0}}, comparator_1_eq};  // Bit_Extender bit_extender_1
  Shifter #(.width(32)) shifter_1 (.in(SrcB), .\dist (5'b10000), .out(shifter_1_out));
  Shifter #(.width(32)) shifter_2 (.in(SrcB), .\dist (shamt), .out(shifter_2_out));
  Comparator #(.width(32)) comparator_2 (.a(SrcA), .b(SrcB), .lt(comparator_2_lt));  // open: gt, eq
  assign bit_extender_2_out = {{31{1'b0}}, comparator_2_lt};  // Bit_Extender bit_extender_2
  Multiplexer #(.select(4), .width(32)) multiplexer_1 (
    .in0(adder_1_out), .in1(subtractor_1_out), .in2(or_1_out), .in3(bit_extender_1_out), .in4(shifter_1_out),
    .in5(shifter_2_out), .in6(bit_extender_2_out), .out(Result), .sel(ALUControl));  // open: in7, in8, in9, in10, in11, in12, in13, in14, in15, en
  Comparator #(.width(32), .mode("unsigned")) comparator_3 (.a(32'h1), .b(Result), .eq(ALUZero));  // open: gt, lt
endmodule

module IM (
  input  [31:0] Addr,
  output [31:0] RD
);

  ROM #(.addrWidth(5), .dataWidth(32)) rom_1 (.addr(Addr[6:2]), .data(RD));  // open: sel

  // Notes on the sheet:
  //   contents of rom_1 (hex, n*v repeats v):
  //   3415000d 3406001e 340c000e 34050016 34080010 34040002 3414001b 3403001e 75d021 11e60001 2f5b823
  //   1b90023 37334a75 accfffb8 8c96001c 35dbf093 3c0d6e1f 3c166ac5 11c00007 ad00ffc8 ac90003c ae8afff8
  //   3c02bfc3 10a50005 35cfb027 0 35cff6de 8d800038 acadffbc 3c12b22d 0 3730aba4
endmodule

module EXT (
  input  [15:0] im16,
  input  Signed,
  output [31:0] ExtOut
);

  wire [31:0] bit_extender_1_out, bit_extender_2_out;

  assign bit_extender_1_out = {{16{1'b0}}, im16};  // Bit_Extender bit_extender_1
  assign bit_extender_2_out = {{16{im16[15]}}, im16};  // Bit_Extender bit_extender_2
  Multiplexer #(.width(32)) multiplexer_1 (
    .in0(bit_extender_1_out), .in1(bit_extender_2_out), .out(ExtOut), .sel(Signed));  // open: en
endmodule

module DM (
  input  [1:0] AddrL_0_1,
  input  [4:0] AddrL_2_6,
  input  [31:0] WD,
  input  [1:0] DMSel,
  input  WE,
  input  clk,
  input  reset,
  output [31:0] RD
);

  wire b0, b1, b2, b3, h0, h1;
  wire [7:0] _0_7, _8_15, _16_23, _24_31, multiplexer_9_out;
  wire [15:0] multiplexer_10_out;
  wire [31:0] multiplexer_5_out, RDb, RDh, WDb, WDh;

  Decoder #(.select(2)) decoder_1 (.out0(b0), .out1(b1), .out2(b2), .out3(b3), .sel(AddrL_0_1));  // open: en
  Multiplexer #(.width(8)) multiplexer_1 (.in0(_0_7), .in1(WD[7:0]), .out(WDb[7:0]), .sel(b0));  // open: en
  Multiplexer #(.width(8)) multiplexer_2 (.in0(_8_15), .in1(WD[7:0]), .out(WDb[15:8]), .sel(b1));  // open: en
  Multiplexer #(.width(8)) multiplexer_3 (.in0(_16_23), .in1(WD[7:0]), .out(WDb[23:16]), .sel(b2));  // open: en
  Multiplexer #(.width(8)) multiplexer_4 (.in0(_24_31), .in1(WD[7:0]), .out(WDb[31:24]), .sel(b3));  // open: en
  Multiplexer #(.select(2), .width(32)) multiplexer_5 (
    .in0(WD), .in1(WDb), .in2(WDh), .out(multiplexer_5_out), .sel(DMSel));  // open: in3, en
  Decoder decoder_2 (.out0(h0), .out1(h1), .sel(AddrL_0_1[1]));  // open: en
  RAM #(.addrWidth(5), .dataWidth(32), .bus("separate")) ram_1 (
    .addr(AddrL_2_6), .din(multiplexer_5_out), .data({_24_31, _16_23, _8_15, _0_7}), .str(WE), .clk(clk),
    .clr(reset));  // open: sel, ld
  Multiplexer #(.width(16)) multiplexer_6 (.in0({_8_15, _0_7}), .in1(WD[15:0]), .out(WDh[15:0]), .sel(h0));  // open: en
  Multiplexer #(.width(16)) multiplexer_7 (
    .in0({_24_31, _16_23}), .in1(WD[15:0]), .out(WDh[31:16]), .sel(h1));  // open: en
  Multiplexer #(.select(2), .width(32)) multiplexer_8 (
    .in0({_24_31, _16_23, _8_15, _0_7}), .in1(RDb), .in2(RDh), .out(RD), .sel(DMSel));  // open: in3, en
  Multiplexer #(.select(2), .width(8)) multiplexer_9 (
    .in0(_0_7), .in1(_8_15), .in2(_16_23), .in3(_24_31), .out(multiplexer_9_out), .sel(AddrL_0_1));  // open: en
  assign RDb = {{24{multiplexer_9_out[7]}}, multiplexer_9_out};  // Bit_Extender bit_extender_1
  assign RDh = {{16{multiplexer_10_out[15]}}, multiplexer_10_out};  // Bit_Extender bit_extender_2
  Multiplexer #(.width(16)) multiplexer_10 (
    .in0({_8_15, _0_7}), .in1({_24_31, _16_23}), .out(multiplexer_10_out), .sel(AddrL_0_1[1]));  // open: en

  // Other names for the same wires on the sheet: RDW[31:0] = {_24_31, _16_23, _8_15, _0_7}
endmodule

module main (
  input  in_1,
  output halt,
  output [31:0] out_3,
  output out_4,
  output [4:0] out_5,
  output [31:0] out_6,
  output out_7,
  output [4:0] out_8,
  output [31:0] out_9
);

  wire ALUZero, clk, ExtOp;
  wire [1:0] A3Sel, DMSel, GWDSel, SrcBSel;
  wire [2:0] NPCSel;
  wire [3:0] ALUControl;
  wire [31:0] ALUOut, DMOut, ext_1_extout, multiplexer_3_out, npc_1_npc, PC4, pc_1_pc, RD1;

  Clock clock_1 (.out(clk));
  NPC npc_1 (
    .ra(RD1), .PC(pc_1_pc), .im26(out_3[25:0]), .im16(out_3[15:0]), .ALUzero(ALUZero), .NPCSel(NPCSel),
    .NPC(npc_1_npc), .PC4(PC4));
  PC pc_1 (.NPC(npc_1_npc), .clk(clk), .reset(in_1), .halt(halt), .PC(pc_1_pc));
  IM im_1 (.Addr(pc_1_pc), .RD(out_3));
  Ctrl ctrl_1 (
    .RD(out_3), .NPCSel(NPCSel), .ExtOp(ExtOp), .GWDSel(GWDSel), .A3Sel(A3Sel), .GWE(out_4),
    .SrcBSel(SrcBSel), .ALUControl(ALUControl), .DWE(out_7), .DMSel(DMSel));
  EXT ext_1 (.im16(out_3[15:0]), .Signed(ExtOp), .ExtOut(ext_1_extout));
  Multiplexer #(.select(2), .width(5)) multiplexer_1 (
    .in0(out_3[15:11]), .in1(out_3[20:16]), .in2({5{1'b1}}), .out(out_5), .sel(A3Sel));  // open: in3, en
  Multiplexer #(.select(2), .width(32)) multiplexer_2 (
    .in0({ALUOut[31:7], out_8, ALUOut[1:0]}), .in1(DMOut), .in2(PC4), .out(out_6), .sel(GWDSel));  // open: in3, en
  GRF grf_1 (
    .A1(out_3[25:21]), .A2(out_3[20:16]), .A3(out_5), .WD(out_6), .clk(clk), .reset(in_1), .WE(out_4),
    .RD1(RD1), .RD2(out_9));
  Multiplexer #(.select(2), .width(32)) multiplexer_3 (
    .in0(out_9), .in1(ext_1_extout), .out(multiplexer_3_out), .sel(SrcBSel));  // open: in2, in3, en
  ALU alu_1 (
    .SrcA(RD1), .SrcB(multiplexer_3_out), .ALUControl(ALUControl), .shamt(out_3[10:6]),
    .Result({ALUOut[31:7], out_8, ALUOut[1:0]}), .ALUZero(ALUZero));
  DM dm_1 (
    .AddrL_0_1(ALUOut[1:0]), .AddrL_2_6(out_8), .WD(out_9), .DMSel(DMSel), .WE(out_7), .clk(clk),
    .reset(in_1), .RD(DMOut));

  // Other names for the same wires on the sheet: A3[4:0] = out_5; ALUOut[6:2] = out_8; DA[4:0] = out_8; DWE = out_7;
  //   GWD[31:0] = out_6; GWE = out_4; im16[15:0] = out_3[15:0]; im26[25:0] = out_3[25:0]; Instr[31:0] = out_3;
  //   shamt[4:0] = out_3[10:6]; RD2[31:0] = out_9; reset = in_1

  // Notes on the sheet:
  //   NPC
  //   PC
  //   IM
  //   Ctrl
  //   im16
  //   offest
  //   rs
  //   base
  //   rt
  //   rd
  //   Ext
  //   GRF
  //   SrcA
  //   ALU
  //   SrcB
  //   DM
endmodule

module NPC (
  input  [31:0] ra,
  input  [31:0] PC,
  input  [25:0] im26,
  input  [15:0] im16,
  input  ALUzero,
  input  [2:0] NPCSel,
  output [31:0] NPC,
  output [31:0] PC4
);

  wire [31:0] adder_2_out, bit_extender_1_out, multiplexer_1_out, shifter_1_out;

  Adder #(.width(32)) adder_1 (.a(PC), .b(32'h4), .out(PC4));  // open: cin, cout
  assign bit_extender_1_out = {{16{im16[15]}}, im16};  // Bit_Extender bit_extender_1
  Shifter #(.width(32)) shifter_1 (.in(bit_extender_1_out), .\dist (5'b00010), .out(shifter_1_out));
  Adder #(.width(32)) adder_2 (.a(shifter_1_out), .b(PC4), .out(adder_2_out));  // open: cin, cout
  Multiplexer #(.width(32)) multiplexer_1 (
    .in0(PC4), .in1(adder_2_out), .out(multiplexer_1_out), .sel(ALUzero));  // open: en
  Multiplexer #(.select(3), .width(32)) multiplexer_2 (
    .in0(PC4), .in1(multiplexer_1_out), .in2({PC[31:28], im26, 2'b00}), .in3(ra), .out(NPC), .sel(NPCSel));  // open: in4, in5, in6, in7, en

  // Notes on the sheet:
  //   offest
endmodule

module PC (
  input  clk,
  input  reset,
  input  [31:0] NPC,
  output [31:0] PC,
  output halt
);

  wire comparator_2_eq, comparator_2_gt, resSel;
  wire [31:0] adder_1_out, register_1_q;

  Register #(.width(32)) register_1 (.D(NPC), .Q(register_1_q), .clk(clk), .clr(reset));  // open: en
  Comparator #(.width(32), .mode("unsigned")) comparator_1 (
    .a({32{1'b0}}), .b(register_1_q), .eq(resSel));  // open: gt, lt
  Adder #(.width(32)) adder_1 (.a(register_1_q), .b({32{1'b0}}), .out(adder_1_out));  // open: cin, cout
  Comparator #(.width(32), .mode("unsigned")) comparator_2 (
    .a(register_1_q), .b(32'h22), .gt(comparator_2_gt), .eq(comparator_2_eq));  // open: lt
  Multiplexer #(.width(32)) multiplexer_1 (.in0(register_1_q), .in1(adder_1_out), .out(PC), .sel(resSel));  // open: en
  or or_1 (halt, comparator_2_gt, comparator_2_eq);
endmodule

module Ctrl (
  input  [31:0] RD,
  output [2:0] NPCSel,
  output ExtOp,
  output [1:0] GWDSel,
  output [1:0] A3Sel,
  output GWE,
  output [1:0] SrcBSel,
  output [3:0] ALUControl,
  output DWE,
  output [1:0] DMSel
);

  wire addu, beq, comparator_2_eq, comparator_3_eq, comparator_4_eq, comparator_5_eq, j, jal, jr, lui, lw,
       ori, R, sll, slti, subu, sw;

  Comparator #(.width(6), .mode("unsigned")) comparator_1 (.a(RD[31:26]), .b({6{1'b0}}), .eq(R));  // open: gt, lt
  Comparator #(.width(6), .mode("unsigned")) comparator_2 (
    .a(RD[5:0]), .b(6'b100001), .eq(comparator_2_eq));  // open: gt, lt
  Comparator #(.width(6), .mode("unsigned")) comparator_3 (
    .a(RD[5:0]), .b(6'b100011), .eq(comparator_3_eq));  // open: gt, lt
  Comparator #(.width(6), .mode("unsigned")) comparator_4 (
    .a(RD[5:0]), .b({6{1'b0}}), .eq(comparator_4_eq));  // open: gt, lt
  Comparator #(.width(6), .mode("unsigned")) comparator_5 (
    .a(RD[5:0]), .b(6'b001000), .eq(comparator_5_eq));  // open: gt, lt
  and and_1 (addu, comparator_2_eq, R);
  and and_2 (subu, comparator_3_eq, R);
  and and_3 (sll, comparator_4_eq, R);
  and and_4 (jr, comparator_5_eq, R);
  buf or_1 (NPCSel[2], 1'b0);  // OR_Gate
  or or_2 (NPCSel[1], jr, jal, j, 1'b0);
  or or_3 (NPCSel[0], jr, beq, 1'b0);
  Comparator #(.width(6), .mode("unsigned")) comparator_6 (.a(RD[31:26]), .b(6'b001101), .eq(ori));  // open: gt, lt
  Comparator #(.width(6), .mode("unsigned")) comparator_7 (.a(RD[31:26]), .b(6'b001111), .eq(lui));  // open: gt, lt
  Comparator #(.width(6), .mode("unsigned")) comparator_8 (.a(RD[31:26]), .b(6'b001010), .eq(slti));  // open: gt, lt
  or or_4 (ExtOp, slti, lw, sw, 1'b0);
  or or_5 (GWDSel[1], jal, 1'b0);
  Comparator #(.width(6), .mode("unsigned")) comparator_9 (.a(RD[31:26]), .b(6'b000100), .eq(beq));  // open: gt, lt
  or or_6 (GWDSel[0], lw, 1'b0);
  or or_7 (A3Sel[1], jal, 1'b0);
  Comparator #(.width(6), .mode("unsigned")) comparator_10 (.a(RD[31:26]), .b(6'b101011), .eq(sw));  // open: gt, lt
  or or_8 (A3Sel[0], slti, lw, lui, ori, 1'b0);
  or or_9 (GWE, 1'b0, lw, lui, ori, subu, addu, 1'b0, jal, slti);
  Comparator #(.width(6), .mode("unsigned")) comparator_11 (.a(RD[31:26]), .b(6'b100011), .eq(lw));  // open: gt, lt
  buf or_10 (SrcBSel[1], 1'b0);  // OR_Gate
  Comparator #(.width(6), .mode("unsigned")) comparator_12 (.a(RD[31:26]), .b(6'b000010), .eq(j));  // open: gt, lt
  Comparator #(.width(6), .mode("unsigned")) comparator_13 (.a(RD[31:26]), .b(6'b000011), .eq(jal));  // open: gt, lt
  or or_11 (SrcBSel[0], slti, ori, lui, sw, lw, 1'b0);
  buf or_12 (ALUControl[3], 1'b0);  // OR_Gate
  or or_13 (ALUControl[2], slti, 1'b0, lui, 1'b0);
  or or_14 (ALUControl[1], slti, beq, ori, 1'b0);
  or or_15 (ALUControl[0], 1'b0, beq, subu, 1'b0);
  or or_16 (DWE, sw, 1'b0);
  buf or_17 (DMSel[1], 1'b0);  // OR_Gate
  buf or_18 (DMSel[0], 1'b0);  // OR_Gate

  // Other names for the same wires on the sheet: func[5:0] = RD[5:0]; op[5:0] = RD[31:26]
endmodule
