// Logisim project D锁.circ as structural Verilog: 2 circuits, main circuit SR
module SR (
  input  R,
  input  S,
  output Q,
  output nQ
);

  nor nor_1 (Q, R, nQ);
  nor nor_2 (nQ, Q, S);
endmodule

module D (
  input  in_1,
  input  in_2,
  output out_3,
  output out_4
);

  wire and_1_out, and_2_out, not_1_out;

  not not_1 (not_1_out, in_2);
  and and_1 (and_1_out, in_1, not_1_out);
  and and_2 (and_2_out, in_1, in_2);
  SR sr_1 (.R(and_1_out), .S(and_2_out), .Q(out_3), .nQ(out_4));
endmodule
