// Logisim project fib1.circ as structural Verilog: 3 circuits, main circuit count
module count (
  input  [2:0] in_1,
  input  in_2,
  output out_3
);

  wire clock_1_out;
  wire [3:0] bit_extender_1_out, counter_1_q;

  // Probe on in_1
  Clock clock_1 (.out(clock_1_out));
  Counter #(.width(4), .max('hf), .ongoal("stay")) counter_1 (
    .D(4'b1111), .Q(counter_1_q), .clk(clock_1_out), .clr(in_2));  // open: load, count, carry
  // Probe on counter_1_q
  assign bit_extender_1_out = {{1{1'b0}}, in_1};  // Bit_Extender bit_extender_1
  Comparator #(.width(4), .mode("unsigned")) comparator_1 (
    .a(bit_extender_1_out), .b(counter_1_q), .lt(out_3));  // open: gt, eq
endmodule

module fib (
  input  in_1,
  input  in_2,
  output [3:0] out_3
);

  wire clock_1_out, clock_2_out, clock_3_out, \判断 ;
  wire [3:0] adder_1_out, multiplexer_1_out, pre;

  Counter #(.width(1), .max('h1), .ongoal("stay")) counter_1 (
    .count(in_1), .Q(\判断 ), .clk(clock_1_out), .clr(in_2));  // open: load, D, carry
  Clock clock_1 (.out(clock_1_out));
  Multiplexer #(.width(4)) multiplexer_1 (.in0(4'b0001), .in1(out_3), .out(multiplexer_1_out), .sel(\判断 ));  // open: en
  Clock clock_2 (.out(clock_2_out));
  Adder #(.width(4)) adder_1 (.a(out_3), .b(pre), .out(adder_1_out));  // open: cin, cout
  Clock clock_3 (.out(clock_3_out));
  Register #(.width(4)) register_1 (.D(multiplexer_1_out), .en(in_1), .Q(pre), .clk(clock_2_out), .clr(in_2));
  Register #(.width(4)) register_2 (.D(adder_1_out), .en(in_1), .Q(out_3), .clk(clock_3_out), .clr(in_2));

  // Other names for the same wires on the sheet: hhh = in_1; now[3:0] = out_3
endmodule

module main (
  input  [2:0] in_1,
  output [3:0] out_2
);

  wire count_1_out_3, not_1_out;
  wire [3:0] fib_1_out_3;

  count count_1 (.in_1(in_1), .in_2(1'b0), .out_3(count_1_out_3));
  not not_1 (not_1_out, count_1_out_3);
  fib fib_1 (.in_1(not_1_out), .in_2(1'b0), .out_3(fib_1_out_3));
  Multiplexer #(.width(4)) multiplexer_1 (
    .in0(4'b0000), .in1(fib_1_out_3), .out(out_2), .sel(count_1_out_3));  // open: en
endmodule
