// Logisim project fib2.circ as structural Verilog: 4 circuits, main circuit 计算乘方
module \矩阵乘法  (
  input  [31:0] A_0_0,
  input  [31:0] A_0_1,
  input  [31:0] A_1_0,
  input  [31:0] A_1_1,
  input  [31:0] B_0_0,
  input  [31:0] B_0_1,
  input  [31:0] B_1_0,
  input  [31:0] B_1_1,
  output [31:0] out_9,
  output [31:0] out_10,
  output [31:0] out_11,
  output [31:0] out_12
);

  wire [31:0] multiplier_1_out, multiplier_2_out, multiplier_3_out, multiplier_4_out, multiplier_5_out,
       multiplier_6_out, multiplier_7_out, multiplier_8_out;

  Multiplier #(.width(32)) multiplier_1 (.a(A_0_0), .b(B_0_0), .out(multiplier_1_out));  // open: cin, cout
  Multiplier #(.width(32)) multiplier_2 (.a(A_0_1), .b(B_1_0), .out(multiplier_2_out));  // open: cin, cout
  Multiplier #(.width(32)) multiplier_3 (.a(A_0_0), .b(B_0_1), .out(multiplier_3_out));  // open: cin, cout
  Multiplier #(.width(32)) multiplier_4 (.a(A_0_1), .b(B_1_1), .out(multiplier_4_out));  // open: cin, cout
  Multiplier #(.width(32)) multiplier_5 (.a(A_1_0), .b(B_0_0), .out(multiplier_5_out));  // open: cin, cout
  Multiplier #(.width(32)) multiplier_6 (.a(A_1_1), .b(B_1_0), .out(multiplier_6_out));  // open: cin, cout
  Multiplier #(.width(32)) multiplier_7 (.a(A_1_0), .b(B_0_1), .out(multiplier_7_out));  // open: cin, cout
  Multiplier #(.width(32)) multiplier_8 (.a(A_1_1), .b(B_1_1), .out(multiplier_8_out));  // open: cin, cout
  Adder #(.width(32)) adder_1 (.a(multiplier_1_out), .b(multiplier_2_out), .out(out_9));  // open: cin, cout
  Adder #(.width(32)) adder_2 (.a(multiplier_3_out), .b(multiplier_4_out), .out(out_10));  // open: cin, cout
  Adder #(.width(32)) adder_3 (.a(multiplier_5_out), .b(multiplier_6_out), .out(out_11));  // open: cin, cout
  Adder #(.width(32)) adder_4 (.a(multiplier_7_out), .b(multiplier_8_out), .out(out_12));  // open: cin, cout
endmodule

module \计算乘方  (
  input  [31:0] in_1,
  input  in_2,
  input  in_3,
  output [31:0] out_4
);

  wire CLK, enable2, init, not_1_out, not_2_out;
  wire [31:0] A_0_0, A_0_1, A_1_0, A_1_1, B_0_0, B_0_1, B_1_1, multiplexer_1_out, multiplexer_6_out,
       multiplexer_7_out, multiplexer_8_out, multiplexer_9_out, now2, register_1_q, register_2_q,
       register_3_q, register_4_q, register_6_q, register_7_q, register_8_q, register_9_q, \矩阵乘法_1_out_9 ,
       \矩阵乘法_1_out_10 , \矩阵乘法_1_out_11 , \矩阵乘法_1_out_12 , \矩阵乘法_2_out_9 , \矩阵乘法_2_out_10 , \矩阵乘法_2_out_11 ,
       \矩阵乘法_2_out_12 ;

  Clock clock_1 (.out(CLK));
  Counter #(.width(1), .max('h1), .ongoal("stay")) counter_1 (
    .carry(init), .clk(CLK), .clr(in_3));  // open: load, D, count, Q
  not not_1 (not_1_out, init);
  Multiplexer #(.width(32)) multiplexer_1 (
    .in0(now2), .in1(in_1), .out(multiplexer_1_out), .sel(not_1_out));  // open: en
  \矩阵乘法  \u_矩阵乘法_1  (
    .A_0_0(A_0_0), .A_0_1(A_0_1), .A_1_0(A_1_0), .A_1_1(A_1_1), .B_0_0(A_0_0), .B_0_1(A_0_1), .B_1_0(A_1_0),
    .B_1_1(A_1_1), .out_9(\矩阵乘法_1_out_9 ), .out_10(\矩阵乘法_1_out_10 ), .out_11(\矩阵乘法_1_out_11 ),
    .out_12(\矩阵乘法_1_out_12 ));
  Register #(.width(32)) register_1 (.D(\矩阵乘法_1_out_9 ), .en(in_2), .Q(register_1_q), .clk(CLK), .clr(in_3));
  Register #(.width(32)) register_2 (.D(\矩阵乘法_1_out_10 ), .en(in_2), .Q(register_2_q), .clk(CLK), .clr(in_3));
  Register #(.width(32)) register_3 (.D(\矩阵乘法_1_out_11 ), .en(in_2), .Q(register_3_q), .clk(CLK), .clr(in_3));
  Register #(.width(32)) register_4 (.D(\矩阵乘法_1_out_12 ), .en(in_2), .Q(register_4_q), .clk(CLK), .clr(in_3));
  Register #(.width(32)) register_5 (
    .D({multiplexer_1_out[0], multiplexer_1_out[31:1]}), .en(in_2), .Q(now2), .clk(CLK), .clr(in_3));
  Comparator #(.width(1), .mode("unsigned")) comparator_1 (
    .a(multiplexer_1_out[0]), .b(1'b1), .eq(enable2));  // open: gt, lt
  Multiplexer #(.width(32)) multiplexer_2 (.in0(32'h1), .in1(register_1_q), .out(A_0_0), .sel(init));  // open: en
  Multiplexer #(.width(32)) multiplexer_3 (.in0(32'h1), .in1(register_2_q), .out(A_0_1), .sel(init));  // open: en
  Multiplexer #(.width(32)) multiplexer_4 (.in0(32'h1), .in1(register_3_q), .out(A_1_0), .sel(init));  // open: en
  Multiplexer #(.width(32)) multiplexer_5 (.in0({32{1'b0}}), .in1(register_4_q), .out(A_1_1), .sel(init));  // open: en
  Multiplexer #(.width(32)) multiplexer_6 (
    .in0(32'h1), .in1(A_0_0), .out(multiplexer_6_out), .sel(enable2));  // open: en
  Multiplexer #(.width(32)) multiplexer_7 (
    .in0({32{1'b0}}), .in1(A_0_1), .out(multiplexer_7_out), .sel(enable2));  // open: en
  Multiplexer #(.width(32)) multiplexer_8 (
    .in0({32{1'b0}}), .in1(A_1_0), .out(multiplexer_8_out), .sel(enable2));  // open: en
  Multiplexer #(.width(32)) multiplexer_9 (
    .in0(32'h1), .in1(A_1_1), .out(multiplexer_9_out), .sel(enable2));  // open: en
  \矩阵乘法  \u_矩阵乘法_2  (
    .A_0_0(B_0_0), .A_0_1(B_0_1), .A_1_0(out_4), .A_1_1(B_1_1), .B_0_0(multiplexer_6_out),
    .B_0_1(multiplexer_7_out), .B_1_0(multiplexer_8_out), .B_1_1(multiplexer_9_out), .out_9(\矩阵乘法_2_out_9 ),
    .out_10(\矩阵乘法_2_out_10 ), .out_11(\矩阵乘法_2_out_11 ), .out_12(\矩阵乘法_2_out_12 ));
  Register #(.width(32)) register_6 (.D(\矩阵乘法_2_out_9 ), .en(in_2), .Q(register_6_q), .clk(CLK), .clr(in_3));
  Register #(.width(32)) register_7 (.D(\矩阵乘法_2_out_10 ), .en(in_2), .Q(register_7_q), .clk(CLK), .clr(in_3));
  Register #(.width(32)) register_8 (.D(\矩阵乘法_2_out_11 ), .en(in_2), .Q(register_8_q), .clk(CLK), .clr(in_3));
  Register #(.width(32)) register_9 (.D(\矩阵乘法_2_out_12 ), .en(in_2), .Q(register_9_q), .clk(CLK), .clr(in_3));
  not not_2 (not_2_out, init);
  Multiplexer #(.width(32)) multiplexer_10 (.in0(register_6_q), .in1(32'h1), .out(B_0_0), .sel(not_2_out));  // open: en
  Multiplexer #(.width(32)) multiplexer_11 (
    .in0(register_7_q), .in1({32{1'b0}}), .out(B_0_1), .sel(not_2_out));  // open: en
  Multiplexer #(.width(32)) multiplexer_12 (
    .in0(register_8_q), .in1({32{1'b0}}), .out(out_4), .sel(not_2_out));  // open: en
  Multiplexer #(.width(32)) multiplexer_13 (.in0(register_9_q), .in1(32'h1), .out(B_1_1), .sel(not_2_out));  // open: en

  // Other names for the same wires on the sheet: B_1_0[31:0] = out_4; enable = in_2; now[31:0] = in_1; reset = in_3
endmodule

module \计数器  (
  input  in_1,
  output out_2
);

  wire clock_1_out, counter_1_carry;

  Clock clock_1 (.out(clock_1_out));
  Counter #(.width(6), .max('h20), .ongoal("stay")) counter_1 (
    .D(6'b100000), .carry(counter_1_carry), .clk(clock_1_out), .clr(in_1));  // open: load, count, Q
  not not_1 (out_2, counter_1_carry);
endmodule

module main (
  input  [31:0] in_1,
  input  in_2,
  output [31:0] out_3
);

  wire \计数器_1_out_2 ;
  wire [31:0] \计算乘方_1_out_4 ;

  \计数器  \u_计数器_1  (.in_1(in_2), .out_2(\计数器_1_out_2 ));
  // Probe on \计算乘方_1_out_4 
  \计算乘方  \u_计算乘方_1  (.in_1(in_1), .in_2(\计数器_1_out_2 ), .in_3(in_2), .out_4(\计算乘方_1_out_4 ));
  Multiplexer #(.width(32)) multiplexer_1 (
    .in0(\计算乘方_1_out_4 ), .in1({32{1'b0}}), .out(out_3), .sel(\计数器_1_out_2 ));  // open: en
endmodule
