// Logisim project logisim_sort4.circ as structural Verilog: 4 circuits, main circuit 1bit_swap
module _1bit_swap (
  input  I1,
  input  I2,
  input  s,
  output O1,
  output O2
);

  wire and_1_out, and_2_out, and_3_out, and_4_out, not_1_out;

  not not_1 (not_1_out, s);
  and and_1 (and_1_out, I1, not_1_out);
  and and_2 (and_2_out, I2, I2, s);
  and and_3 (and_3_out, I2, not_1_out);
  and and_4 (and_4_out, I1, s);
  or or_1 (O1, and_1_out, and_2_out);
  or or_2 (O2, and_3_out, and_4_out);
endmodule

module _4bit_swap (
  input  [3:0] in_1,
  input  [3:0] in_2,
  input  in_3,
  output [3:0] out_4,
  output [3:0] out_5
);

  _1bit_swap u_1bit_swap_1 (.I1(in_1[0]), .I2(in_2[0]), .s(in_3), .O1(out_4[0]), .O2(out_5[0]));
  _1bit_swap u_1bit_swap_2 (.I1(in_1[1]), .I2(in_2[1]), .s(in_3), .O1(out_4[1]), .O2(out_5[1]));
  _1bit_swap u_1bit_swap_3 (.I1(in_1[2]), .I2(in_2[2]), .s(in_3), .O1(out_4[2]), .O2(out_5[2]));
  _1bit_swap u_1bit_swap_4 (.I1(in_1[3]), .I2(in_2[3]), .s(in_3), .O1(out_4[3]), .O2(out_5[3]));

  // Other names for the same wires on the sheet: HHH = in_3; a0_t = in_1[0]; a1_t = in_1[1]; a2_t = in_1[2];
  //   a3_t = in_1[3]; b0_t = in_2[0]; b1_t = in_2[1]; b2_t = in_2[2]; b3_t = in_2[3]; A0 = out_4[0]; A1 = out_4[1];
  //   A2 = out_4[2]; A3 = out_4[3]; B0 = out_5[0]; B1 = out_5[1]; B2 = out_5[2]; B3 = out_5[3]
endmodule

module _4bit2_sort (
  input  [3:0] in_1,
  input  [3:0] in_2,
  output [3:0] out_3,
  output [3:0] out_4
);

  wire comparator_1_gt;

  Comparator #(.width(4), .mode("unsigned")) comparator_1 (.a(in_1), .b(in_2), .gt(comparator_1_gt));  // open: eq, lt
  _4bit_swap u_4bit_swap_1 (.in_1(in_1), .in_2(in_2), .in_3(comparator_1_gt), .out_4(out_3), .out_5(out_4));
endmodule

module _4bit_sort (
  input  [3:0] in_1,
  input  [3:0] in_2,
  input  [3:0] in_3,
  input  [3:0] in_4,
  output [3:0] out_5,
  output [3:0] out_6,
  output [3:0] out_7,
  output [3:0] out_8
);

  wire [3:0] n4bit2_sort_1_out_3, n4bit2_sort_1_out_4, n4bit2_sort_2_out_3, n4bit2_sort_2_out_4,
       n4bit2_sort_3_out_4, n4bit2_sort_4_out_3;

  _4bit2_sort u_4bit2_sort_1 (.in_1(in_1), .in_2(in_2), .out_3(n4bit2_sort_1_out_3), .out_4(n4bit2_sort_1_out_4));
  _4bit2_sort u_4bit2_sort_2 (.in_1(in_3), .in_2(in_4), .out_3(n4bit2_sort_2_out_3), .out_4(n4bit2_sort_2_out_4));
  _4bit2_sort u_4bit2_sort_3 (
    .in_1(n4bit2_sort_1_out_3), .in_2(n4bit2_sort_2_out_3), .out_3(out_5), .out_4(n4bit2_sort_3_out_4));
  _4bit2_sort u_4bit2_sort_4 (
    .in_1(n4bit2_sort_1_out_4), .in_2(n4bit2_sort_2_out_4), .out_3(n4bit2_sort_4_out_3), .out_4(out_8));
  _4bit2_sort u_4bit2_sort_5 (.in_1(n4bit2_sort_3_out_4), .in_2(n4bit2_sort_4_out_3), .out_3(out_6), .out_4(out_7));
endmodule
