// Logisim project logisim_swap.circ as structural Verilog: 1 circuit, main circuit swap
module swap (
  input  I1,
  input  I2,
  input  s,
  output O1,
  output O2
);

  wire and_1_out, and_2_out, and_3_out, and_4_out, not_1_out;

  not not_1 (not_1_out, s);
  and and_1 (and_1_out, I1, not_1_out);
  and and_2 (and_2_out, I2, I2, s);
  and and_3 (and_3_out, I2, not_1_out);
  and and_4 (and_4_out, I1, s);
  or or_1 (O1, and_1_out, and_2_out);
  or or_2 (O2, and_3_out, and_4_out);
endmodule
